# Fritzing sketch ESP32-3-connector (saved by Fritzing 1.0.6)
circuit board: 5.48816cm x 8.02077cm
breadboards: 1

parts:
  ESP32-S30Wroom-board = ESP32-S3-Wroom-board-Freenove_1
  +_- = Camdenboss CTB0158-2 [part_number=CTB0158-2 package=THT]
  42_41 = Camdenboss CTB0158-2 [part_number=CTB0158-2 package=THT]
  42_42 = Camdenboss CTB0158-2 [part_number=CTB0158-2 package=THT]

nets:
  N1: ESP32-S30Wroom-board.connector0, +_-.pin1
  N2: ESP32-S30Wroom-board.connector20, +_-.pin2
  N3: ESP32-S30Wroom-board.connector34, 42_42.pin2
  N4: ESP32-S30Wroom-board.connector35, 42_42.pin1
  N5: ESP32-S30Wroom-board.connector36, 42_41.pin1
  N6: ESP32-S30Wroom-board.connector37, 42_41.pin2
