# Fritzing sketch ESP32-3-connector (saved by Fritzing 1.0.6)
circuit board: 5.48816cm x 8.02077cm
breadboards: 1

parts:
  ESP32-S30Wroom-board = ESP32-S3 Wroom board Freenove
  2_1 = Camdenboss CTB0158-2 [part_number=CTB0158-2 package=THT]
  42_41 = Camdenboss CTB0158-2 [part_number=CTB0158-2 package=THT]
  -_+ = Camdenboss CTB0158-2 [part_number=CTB0158-2 package=THT]

nets:
  N1: ESP32-S30Wroom-board.Pin_3, 2_1.pin2
  N2: ESP32-S30Wroom-board.Pin_4, 2_1.pin1
  N3: ESP32-S30Wroom-board.Pin_5, 42_41.pin1
  N4: ESP32-S30Wroom-board.Pin_6, 42_41.pin2
  N5: ESP32-S30Wroom-board.Pin_20, -_+.pin1
  N6: ESP32-S30Wroom-board.Pin_40, -_+.pin2

notes:
  Version
  {version}

custom parts:
  ESP32-S3 Wroom board Freenove: ESP32-S3-WROOM is a powerful and small controller with onboard wireless and camera.
